# Fritzing sketch casio2ftdi (saved by Fritzing 0.9.9b)
circuit board: 3.89222cm x 1.70018cm

parts:
  ftdi_header = mystery part, 6 pins [chip_label=?]
  bottom_row = female pin header, 15 pins [form="♀ (female)"]
  top_row = female pin header, 15 pins [form="♀ (female)"]
  RX = smd LED [color="Green (565nm)" current=0.030 package="0805 [SMD]"]
  TX = smd LED [color="Blue (470nm)" current=0.030 package="0805 [SMD]"]
  R3 = Resistor [tolerance=±5% resistance=1k power=0.25 package="0805 [SMD]"]
  R3_2 = Resistor [tolerance=±5% resistance=1k power=0.25 package="0805 [SMD]"]
  R2 = Resistor [tolerance=±5% resistance=0 power=0.25 package="0805 [SMD]"]
  R1 = Resistor [tolerance=±5% resistance=50 power=0.25 package="0805 [SMD]"]

nets:
  GND: ftdi_header.pin1, bottom_row.pin1
  5V: ftdi_header.pin2, R2.Pin_1, R1.Pin_1
  RX: ftdi_header.pin3, top_row.pin11, R3.Pin_0
  TX: ftdi_header.pin4, bottom_row.pin9, R3_2.Pin_0
  RTS: ftdi_header.pin5, top_row.pin9
  CTS: ftdi_header.pin6, bottom_row.pin14
  N1: RX.cathode, R3.Pin_1
  N2: RX.anode, R1.Pin_0
  N3: TX.cathode, R3_2.Pin_1
  N4: TX.anode, R2.Pin_0

notes:
  v3
  TX RTS CTS
  GND 5V RX
  FTDI-FX
  LH-9/21
  JLCJLCJLCJLC
  30 pin, 2-row right-angle 1.27mm pitch header
  0.7mm hole, 0.22mm copper ring
  PCB thickness: 1.2mm
